// Logisim project epu_educational.circ as structural Verilog: 4 circuits, main circuit main
module main (
);

  wire clock_1_out, decode_1_acc_enable, decode_1_arith_mode, decode_1_control_mode, decode_1_rreg_enable,
       decode_1_wreg_enable;
  wire [1:0] decode_1_opcode;
  wire [3:0] decode_1_reg_num;
  wire [7:0] arith_1_acc_out, control_1_pc, ram_1_dout, rom_1_data;

  Clock clock_1 (.out(clock_1_out));
  ROM rom_1 (.addr(control_1_pc), .data(rom_1_data));
  CONTROL control_1 (
    .CONTROL_MODE(decode_1_control_mode), .CLK(clock_1_out), .OPCODE(decode_1_opcode),
    .ACC_IN(arith_1_acc_out), .REG_IN(ram_1_dout), .PC(control_1_pc));
  DECODE decode_1 (
    .INSTRUCTION(rom_1_data), .CLK(clock_1_out), .CONTROL_MODE(decode_1_control_mode),
    .ARITH_MODE(decode_1_arith_mode), .ACC_ENABLE(decode_1_acc_enable), .WREG_ENABLE(decode_1_wreg_enable),
    .RREG_ENABLE(decode_1_rreg_enable), .OPCODE(decode_1_opcode), .REG_NUM(decode_1_reg_num));
  RAM #(.addrWidth(4), .asyncread("true")) ram_1 (
    .addr(decode_1_reg_num), .we(decode_1_wreg_enable), .oe(decode_1_rreg_enable), .clk(clock_1_out),
    .din(arith_1_acc_out), .dout(ram_1_dout));
  ARITH arith_1 (
    .OPCODE(decode_1_opcode), .IMM_IN(rom_1_data), .ARITH_MODE(decode_1_arith_mode),
    .ACC_ENABLE(decode_1_acc_enable), .CLK(clock_1_out), .REG_IN(ram_1_dout), .ACC_OUT(arith_1_acc_out));

  // Notes on the sheet:
  //   contents of rom_1 (hex, n*v repeats v):
  //   0 3 2 0 5 1 12 0 ff f2 0 8 15 fb 241*0 f9
endmodule

module DECODE (
  input  [7:0] INSTRUCTION,
  input  CLK,
  output CONTROL_MODE,
  output ARITH_MODE,
  output ACC_ENABLE,
  output WREG_ENABLE,
  output RREG_ENABLE,
  output [1:0] OPCODE,
  output [3:0] REG_NUM
);

  wire and_4_out, and_5_out, decoder_1_out0, decoder_1_out1, decoder_1_out2, not_1_out, not_2_out, t_ff_1_q;
  wire [3:0] multiplexer_1_out;
  wire [7:0] register_1_q;

  not not_1 (not_1_out, t_ff_1_q);
  Register register_1 (.D(INSTRUCTION), .en(not_1_out), .clk(CLK), .Q(register_1_q));  // open: clr
  Multiplexer #(.enable("false"), .width(8)) multiplexer_1 (
    .in0(INSTRUCTION), .in1(register_1_q),
    .out({REG_NUM, multiplexer_1_out[3], OPCODE, multiplexer_1_out[0]}), .sel(t_ff_1_q));
  not not_2 (not_2_out, multiplexer_1_out[0]);
  and and_1 (ARITH_MODE, multiplexer_1_out[0], ~multiplexer_1_out[3]);  // AND_Gate
  and and_2 (CONTROL_MODE, multiplexer_1_out[0], multiplexer_1_out[3]);
  Decoder #(.enable("false"), .select(2)) decoder_1 (
    .out0(decoder_1_out0), .out1(decoder_1_out1), .out2(decoder_1_out2), .sel(OPCODE));  // open: out3
  and and_3 (WREG_ENABLE, not_2_out, decoder_1_out1);
  and and_4 (and_4_out, decoder_1_out2, not_2_out);
  T_Flip_Flop t_ff_1 (.T(and_5_out), .clk(CLK), .Q(t_ff_1_q));  // open: Qn, reset, preset
  and and_5 (and_5_out, not_2_out, decoder_1_out0);
  or or_1 (ACC_ENABLE, t_ff_1_q, and_4_out, ARITH_MODE);
  or or_2 (RREG_ENABLE, ARITH_MODE, and_4_out);

  // Notes on the sheet:
  //   MEMORY MODE
  //   ARITH MODE
  //   CONTROL MODE
  //   IS LDI
endmodule

module ARITH (
  input  [1:0] OPCODE,
  input  [7:0] IMM_IN,
  input  ARITH_MODE,
  input  ACC_ENABLE,
  input  CLK,
  input  [7:0] REG_IN,
  output [7:0] ACC_OUT
);

  wire [7:0] adder_1_out, multiplexer_1_out, multiplexer_2_out, multiplexer_3_out, pull_resistor_1_node,
       pull_resistor_2_node, subtractor_1_out;

  Multiplexer #(.enable("false"), .select(2), .width(8)) multiplexer_1 (
    .in0(IMM_IN), .in2(REG_IN), .out(multiplexer_1_out), .sel(OPCODE));  // open: in1, in3
  Multiplexer #(.enable("false"), .width(8)) multiplexer_2 (
    .in0(multiplexer_1_out), .in1(multiplexer_3_out), .out(multiplexer_2_out), .sel(ARITH_MODE));
  Register register_1 (.D(multiplexer_2_out), .en(ACC_ENABLE), .clk(CLK), .Q(ACC_OUT));  // open: clr
  Adder adder_1 (.a(ACC_OUT), .b(REG_IN), .out(adder_1_out));  // open: cin, cout
  Subtractor subtractor_1 (.a(ACC_OUT), .b(REG_IN), .out(subtractor_1_out));  // open: bin, bout
  Pull_Resistor pull_resistor_1 (.node(pull_resistor_1_node));
  Pull_Resistor pull_resistor_2 (.node(pull_resistor_2_node));
  Comparator comparator_1 (
    .a(ACC_OUT), .b(REG_IN), .eq(pull_resistor_1_node[0]), .lt(pull_resistor_2_node[0]));  // open: gt
  Multiplexer #(.enable("false"), .select(2), .width(8)) multiplexer_3 (
    .in0(adder_1_out), .in1(subtractor_1_out), .in2(pull_resistor_1_node), .in3(pull_resistor_2_node),
    .out(multiplexer_3_out), .sel(OPCODE));
endmodule

module CONTROL (
  input  CONTROL_MODE,
  input  CLK,
  input  [1:0] OPCODE,
  input  [7:0] ACC_IN,
  input  [7:0] REG_IN,
  output [7:0] PC
);

  wire and_1_out, and_2_out, comparator_1_eq, decoder_1_out1, decoder_1_out2;
  wire [7:0] adder_1_out, multiplexer_1_out, multiplexer_2_out, multiplexer_3_out, multiplexer_4_out;

  Decoder #(.enable("false"), .select(2)) decoder_1 (
    .out1(decoder_1_out1), .out2(decoder_1_out2), .sel(OPCODE));  // open: out0, out3
  Comparator comparator_1 (.a(ACC_IN), .b({8{1'b0}}), .eq(comparator_1_eq));  // open: gt, lt
  and and_1 (and_1_out, comparator_1_eq, decoder_1_out2);
  and and_2 (and_2_out, ~comparator_1_eq, decoder_1_out1);  // AND_Gate
  Multiplexer #(.enable("false"), .width(8)) multiplexer_1 (
    .in0(PC), .in1(REG_IN), .out(multiplexer_1_out), .sel(and_1_out));
  Multiplexer #(.enable("false"), .width(8)) multiplexer_2 (
    .in0(PC), .in1(REG_IN), .out(multiplexer_2_out), .sel(and_2_out));
  Adder adder_1 (.a(PC), .b(8'h1), .out(adder_1_out));  // open: cin, cout
  Multiplexer #(.enable("false"), .width(8)) multiplexer_3 (
    .in0(adder_1_out), .in1(multiplexer_4_out), .out(multiplexer_3_out), .sel(CONTROL_MODE));
  Multiplexer #(.enable("false"), .select(2), .width(8)) multiplexer_4 (
    .in0(REG_IN), .in1(multiplexer_2_out), .in2(multiplexer_1_out), .in3(adder_1_out),
    .out(multiplexer_4_out), .sel(OPCODE));
  Register register_1 (.D(multiplexer_3_out), .clk(CLK), .Q(PC));  // open: en, clr
endmodule
