// Logisim project epu2.circ as structural Verilog: 8 circuits, main circuit regFile
module main (
);

  wire and_1_out, and_2_out, and_3_out, and_4_out, and_5_out, and_6_out, comparator_1_eq, comparator_1_lt,
       cu_1_alu, cu_1_copy, cu_1_ji, cu_1_jlz, cu_1_jnz, cu_1_jx, cu_1_jz, cu_1_ldi, cu_1_load, cu_1_save,
       cu_1_stallde, cu_1_stallex, cu_1_stallif, cu_1_store, deex_1_out_16, deex_1_out_17, deex_1_out_18,
       deex_1_out_19, deex_1_out_20, deex_1_out_21, deex_1_out_22, deex_1_out_23, deex_1_out_24,
       memory_1_ack, mmapDevices, mmapVram, nor_1_out, not_1_out, not_2_out, not_3_out, or_1_out, or_2_out,
       or_3_out, or_4_out, sharedClk, sharedRst;
  wire [3:0] cu_1_opcode, cu_1_regnr, deex_1_out_25, deex_1_out_26;
  wire [31:0] adder_1_out, adder_2_out, alu_1_c, controlled_buffer_1_out, controlled_buffer_5_out, cu_1_imm,
       deex_1_out_27, memory_1_dataout, mmapAddr, mmapDataIn, mmapDataOut, multiplexer_1_out,
       regfile_1_readval, register_1_q, register_2_q, register_3_q, rom_1_data;

  nor nor_1 (nor_1_out, or_3_out, cu_1_ji, cu_1_jx);
  assign controlled_buffer_1_out = nor_1_out ? adder_1_out : 32'bz;  // Controlled_Buffer controlled_buffer_1
  Adder #(.width(32)) adder_1 (.a(register_1_q), .b(32'h1), .out(adder_1_out));  // open: cin, cout
  assign controlled_buffer_1_out = or_3_out ? mmapAddr : 32'bz;  // Controlled_Buffer controlled_buffer_2
  assign controlled_buffer_1_out = cu_1_jx ? adder_2_out : 32'bz;  // Controlled_Buffer controlled_buffer_3
  assign controlled_buffer_1_out = cu_1_ji ? regfile_1_readval : 32'bz;  // Controlled_Buffer controlled_buffer_4
  Register #(.width(32)) register_1 (
    .D(controlled_buffer_1_out), .en(not_1_out), .clk(sharedClk), .Q(register_1_q), .clr(sharedRst));
  not not_1 (not_1_out, cu_1_stallif);
  ROM #(.addrWidth(24), .dataWidth(32)) rom_1 (.addr(register_1_q[23:0]), .data(rom_1_data));
  Register #(.width(32)) register_2 (
    .D(rom_1_data), .en(not_2_out), .clk(sharedClk), .Q(register_2_q), .clr(sharedRst));
  not not_2 (not_2_out, cu_1_stallde);
  Register #(.width(32)) register_3 (
    .D(register_1_q), .en(not_2_out), .clk(sharedClk), .Q(register_3_q), .clr(sharedRst));
  Adder #(.width(32)) adder_2 (.a(register_3_q), .b(cu_1_imm), .out(adder_2_out));  // open: cin, cout
  // RGB_Video rgb_video_1: pin names not known; wires that end beside it: sharedRst, sharedClk, mmapVram, mmapAddr[13:7], mmapAddr[6:0], mmapDataIn[23:0]
  Clock clock_1 (.out(sharedClk));
  Button button_1 (.out(sharedRst));
  and and_1 (and_1_out, ~cu_1_stallde, deex_1_out_21);  // AND_Gate
  CU cu_1 (
    .memAck(memory_1_ack), .ctlAck(or_4_out), .termIn(register_2_q), .clk(sharedClk), .rst(sharedRst),
    .stallIF(cu_1_stallif), .stallDE(cu_1_stallde), .stallEX(cu_1_stallex), .alu(cu_1_alu), .ldi(cu_1_ldi),
    .load(cu_1_load), .store(cu_1_store), .copy(cu_1_copy), .save(cu_1_save), .jx(cu_1_jx), .ji(cu_1_ji),
    .jz(cu_1_jz), .jnz(cu_1_jnz), .jlz(cu_1_jlz), .opcode(cu_1_opcode), .regNr(cu_1_regnr), .imm(cu_1_imm));
  regFile regfile_1 (
    .writeEna(and_1_out), .readNr(cu_1_regnr), .writeNr(deex_1_out_26), .writeVal(mmapDataIn),
    .clk(sharedClk), .rst(sharedRst), .readVal(regfile_1_readval));
  not not_3 (not_3_out, cu_1_stallex);
  Register #(.width(32)) register_4 (
    .D(regfile_1_readval), .en(not_3_out), .clk(sharedClk), .Q(mmapAddr), .clr(sharedRst));
  DEEX deex_1 (
    .in_1(cu_1_alu), .in_2(cu_1_ldi), .in_3(cu_1_load), .in_4(cu_1_store), .in_5(cu_1_copy),
    .in_6(cu_1_save), .in_7(cu_1_jz), .in_8(cu_1_jnz), .in_9(cu_1_jlz), .in_10(cu_1_opcode),
    .in_11(cu_1_regnr), .in_12(cu_1_imm), .stall(cu_1_stallex), .clk(sharedClk), .rst(sharedRst),
    .out_16(deex_1_out_16), .out_17(deex_1_out_17), .out_18(deex_1_out_18), .out_19(deex_1_out_19),
    .out_20(deex_1_out_20), .out_21(deex_1_out_21), .out_22(deex_1_out_22), .out_23(deex_1_out_23),
    .out_24(deex_1_out_24), .out_25(deex_1_out_25), .out_26(deex_1_out_26), .out_27(deex_1_out_27));
  Multiplexer #(.width(32)) multiplexer_1 (
    .in0(mmapAddr), .in1(deex_1_out_27), .out(multiplexer_1_out), .sel(deex_1_out_17));
  memory memory_1 (
    .mmapData(mmapDataOut), .load(deex_1_out_18), .store(deex_1_out_19), .addr(mmapAddr),
    .dataIn(mmapDataIn), .clk(sharedClk), .mmapDevices(mmapDevices), .mmapVram(mmapVram), .ack(memory_1_ack),
    .dataOut(memory_1_dataout));
  alu alu_1 (.opSel(deex_1_out_25), .a(mmapDataIn), .b(multiplexer_1_out), .c(alu_1_c));
  assign controlled_buffer_5_out = or_1_out ? multiplexer_1_out : 32'bz;  // Controlled_Buffer controlled_buffer_5
  or or_1 (or_1_out, deex_1_out_17, deex_1_out_20);
  assign controlled_buffer_5_out = deex_1_out_16 ? alu_1_c : 32'bz;  // Controlled_Buffer controlled_buffer_6
  assign controlled_buffer_5_out = deex_1_out_18 ? memory_1_dataout : 32'bz;  // Controlled_Buffer controlled_buffer_7
  and and_2 (and_2_out, memory_1_ack, deex_1_out_18);
  or or_2 (or_2_out, and_2_out, deex_1_out_16, or_1_out);
  Register #(.width(32)) register_5 (
    .D(controlled_buffer_5_out), .en(and_3_out), .clk(sharedClk), .Q(mmapDataIn), .clr(sharedRst));
  Pull_Resistor pull_resistor_1 (.node(controlled_buffer_5_out));
  and and_3 (and_3_out, or_2_out, ~cu_1_stallex);  // AND_Gate
  Comparator #(.width(32)) comparator_1 (
    .a(mmapDataIn), .b({32{1'b0}}), .eq(comparator_1_eq), .lt(comparator_1_lt));  // open: gt
  and and_4 (and_4_out, comparator_1_eq, deex_1_out_22);
  and and_5 (and_5_out, ~comparator_1_eq, deex_1_out_23);  // AND_Gate
  and and_6 (and_6_out, comparator_1_lt, deex_1_out_24);
  or or_3 (or_3_out, and_4_out, and_5_out, and_6_out);
  or or_4 (or_4_out, deex_1_out_22, deex_1_out_23, deex_1_out_24);

  // Notes on the sheet:
  //   contents of rom_1 (hex, n*v repeats v):
  //   0 f13 50000 113 30000 141 f38
endmodule

module CU (
  input  memAck,
  input  ctlAck,
  input  [31:0] termIn,
  input  clk,
  input  rst,
  output stallIF,
  output stallDE,
  output stallEX,
  output alu,
  output ldi,
  output load,
  output store,
  output copy,
  output save,
  output jx,
  output ji,
  output jz,
  output jnz,
  output jlz,
  output [3:0] opcode,
  output [3:0] regNr,
  output [31:0] imm
);

  wire or_1_out, or_2_out;

  opDecode opdecode_1 (
    .op(termIn[7:0]), .aluOp(alu), .ldiOp(ldi), .loadOp(load), .storeOp(store), .copyOp(copy), .saveOp(save),
    .jxOp(jx), .jiOp(ji), .jzOp(jz), .jnzOp(jnz), .jlzOp(jlz));
  assign imm = {{16{termIn[31]}}, termIn[31:16]};  // Bit_Extender bit_extender_1
  or or_1 (or_1_out, load, store);
  or or_2 (or_2_out, jz, jnz, jlz);
  stallMgr stallmgr_1 (
    .memOp(or_1_out), .memAck(memAck), .ctlOp(or_2_out), .ctlAck(ctlAck), .clk(clk), .rst(rst),
    .stallIF(stallIF), .stallDE(stallDE), .stallEX(stallEX));

  assign opcode = termIn[7:4];
  assign regNr = termIn[11:8];
endmodule

module stallMgr (
  input  memOp,
  input  memAck,
  input  ctlOp,
  input  ctlAck,
  input  clk,
  input  rst,
  output stallIF,
  output stallDE,
  output stallEX
);

  wire and_1_out, and_2_out, and_3_out, and_4_out, or_1_out, or_2_out, or_3_out, or_4_out, register_1_q,
       register_2_q;

  and and_1 (and_1_out, memOp, ~memAck);  // AND_Gate
  and and_2 (and_2_out, ctlOp, ~ctlAck);  // AND_Gate
  and and_3 (and_3_out, register_1_q, ~memAck);  // AND_Gate
  and and_4 (and_4_out, register_2_q, ~ctlAck);  // AND_Gate
  Register #(.width(1)) register_1 (.D(or_1_out), .clk(clk), .Q(register_1_q), .clr(rst));  // open: en
  or or_1 (or_1_out, memOp, and_3_out);
  Register #(.width(1)) register_2 (.D(or_2_out), .clk(clk), .Q(register_2_q), .clr(rst));  // open: en
  or or_2 (or_2_out, ctlOp, and_4_out);
  or or_3 (or_3_out, and_1_out, register_1_q);
  or or_4 (or_4_out, and_2_out, register_2_q);
  or or_5 (stallDE, register_1_q, register_2_q);
  or or_6 (stallEX, register_1_q, register_2_q);
  or or_7 (stallIF, or_3_out, or_4_out);

  // Notes on the sheet:
  //   TODO: Figure out other stall conditions?
endmodule

module opDecode (
  input  [7:0] op,
  output aluOp,
  output ldiOp,
  output loadOp,
  output storeOp,
  output copyOp,
  output saveOp,
  output jxOp,
  output jiOp,
  output jzOp,
  output jnzOp,
  output jlzOp
);

  wire jmp_out, mem_out, mov_out;

  nor mem (mem_out, op[0], op[3]);
  and mov (mov_out, op[0], op[1]);
  and jmp (jmp_out, ~op[0], op[3]);  // AND_Gate
  and alu (aluOp, op[0], ~op[1]);  // AND_Gate
  and ldi (ldiOp, mem_out, ~op[4], ~op[5]);  // AND_Gate
  and lod (loadOp, mem_out, op[4], ~op[5]);  // AND_Gate
  and str (storeOp, mem_out, ~op[4], op[5]);  // AND_Gate
  and cpy (copyOp, mov_out, ~op[4], ~op[5]);  // AND_Gate
  and sav (saveOp, mov_out, op[4], ~op[5]);  // AND_Gate
  and jx (jxOp, jmp_out, ~op[4], ~op[5]);  // AND_Gate
  and ji (jiOp, jmp_out, ~op[4], op[5]);  // AND_Gate
  and jz (jzOp, jmp_out, op[4], ~op[5]);  // AND_Gate
  and jnz (jnzOp, jmp_out, op[4], op[5]);
  and jlz (jlzOp, jmp_out, op[4], op[6]);
endmodule

module regFile (
  input  writeEna,
  input  [3:0] readNr,
  input  [3:0] writeNr,
  input  [31:0] writeVal,
  input  clk,
  input  rst,
  output [31:0] readVal
);

  wire decoder_1_out0, decoder_1_out1, decoder_1_out2, decoder_1_out3, decoder_1_out4, decoder_1_out5,
       decoder_1_out6, decoder_1_out7, decoder_1_out8, decoder_1_out9, decoder_1_out10, decoder_1_out11,
       decoder_1_out12, decoder_1_out13, decoder_1_out14, decoder_1_out15;
  wire [31:0] register_1_q, register_2_q, register_3_q, register_4_q, register_5_q, register_6_q,
       register_7_q, register_8_q, register_9_q, register_10_q, register_11_q, register_12_q, register_13_q,
       register_14_q, register_15_q, register_16_q;

  Decoder #(.select(4)) decoder_1 (
    .out0(decoder_1_out0), .out1(decoder_1_out1), .out2(decoder_1_out2), .out3(decoder_1_out3),
    .out4(decoder_1_out4), .out5(decoder_1_out5), .out6(decoder_1_out6), .out7(decoder_1_out7),
    .out8(decoder_1_out8), .out9(decoder_1_out9), .out10(decoder_1_out10), .out11(decoder_1_out11),
    .out12(decoder_1_out12), .out13(decoder_1_out13), .out14(decoder_1_out14), .out15(decoder_1_out15),
    .sel(writeNr), .en(writeEna));
  Register #(.width(32)) register_1 (.D(writeVal), .en(decoder_1_out0), .clk(clk), .Q(register_1_q), .clr(rst));
  Register #(.width(32)) register_2 (.D(writeVal), .en(decoder_1_out1), .clk(clk), .Q(register_2_q), .clr(rst));
  Register #(.width(32)) register_3 (.D(writeVal), .en(decoder_1_out2), .clk(clk), .Q(register_3_q), .clr(rst));
  Register #(.width(32)) register_4 (.D(writeVal), .en(decoder_1_out3), .clk(clk), .Q(register_4_q), .clr(rst));
  Register #(.width(32)) register_5 (.D(writeVal), .en(decoder_1_out4), .clk(clk), .Q(register_5_q), .clr(rst));
  Register #(.width(32)) register_6 (.D(writeVal), .en(decoder_1_out5), .clk(clk), .Q(register_6_q), .clr(rst));
  Register #(.width(32)) register_7 (.D(writeVal), .en(decoder_1_out6), .clk(clk), .Q(register_7_q), .clr(rst));
  Register #(.width(32)) register_8 (.D(writeVal), .en(decoder_1_out7), .clk(clk), .Q(register_8_q), .clr(rst));
  Register #(.width(32)) register_9 (.D(writeVal), .en(decoder_1_out8), .clk(clk), .Q(register_9_q), .clr(rst));
  Register #(.width(32)) register_10 (.D(writeVal), .en(decoder_1_out9), .clk(clk), .Q(register_10_q), .clr(rst));
  Register #(.width(32)) register_11 (.D(writeVal), .en(decoder_1_out10), .clk(clk), .Q(register_11_q), .clr(rst));
  Register #(.width(32)) register_12 (.D(writeVal), .en(decoder_1_out11), .clk(clk), .Q(register_12_q), .clr(rst));
  Register #(.width(32)) register_13 (.D(writeVal), .en(decoder_1_out12), .clk(clk), .Q(register_13_q), .clr(rst));
  Register #(.width(32)) register_14 (.D(writeVal), .en(decoder_1_out13), .clk(clk), .Q(register_14_q), .clr(rst));
  Register #(.width(32)) register_15 (.D(writeVal), .en(decoder_1_out14), .clk(clk), .Q(register_15_q), .clr(rst));
  Register #(.width(32)) register_16 (.D(writeVal), .en(decoder_1_out15), .clk(clk), .Q(register_16_q), .clr(rst));
  Multiplexer #(.select(4), .width(32)) multiplexer_1 (
    .in0(register_1_q), .in1(register_2_q), .in2(register_3_q), .in3(register_4_q), .in4(register_5_q),
    .in5(register_6_q), .in6(register_7_q), .in7(register_8_q), .in8(register_9_q), .in9(register_10_q),
    .in10(register_11_q), .in11(register_12_q), .in12(register_13_q), .in13(register_14_q),
    .in14(register_15_q), .in15(register_16_q), .out(readVal), .sel(readNr));
endmodule

module DEEX (
  input  in_1,
  input  in_2,
  input  in_3,
  input  in_4,
  input  in_5,
  input  in_6,
  input  in_7,
  input  in_8,
  input  in_9,
  input  [3:0] in_10,
  input  [3:0] in_11,
  input  [31:0] in_12,
  input  stall,
  input  clk,
  input  rst,
  output out_16,
  output out_17,
  output out_18,
  output out_19,
  output out_20,
  output out_21,
  output out_22,
  output out_23,
  output out_24,
  output [3:0] out_25,
  output [3:0] out_26,
  output [31:0] out_27
);

  wire not_1_out, register_13_q;

  Register #(.width(1)) register_1 (.D(in_1), .en(not_1_out), .clk(clk), .Q(out_16), .clr(rst));
  Register #(.width(1)) register_2 (.D(in_2), .en(not_1_out), .clk(clk), .Q(out_17), .clr(rst));
  Register #(.width(1)) register_3 (.D(in_3), .en(not_1_out), .clk(clk), .Q(out_18), .clr(rst));
  Register #(.width(1)) register_4 (.D(in_4), .en(not_1_out), .clk(clk), .Q(out_19), .clr(rst));
  Register #(.width(1)) register_5 (.D(in_5), .en(not_1_out), .clk(clk), .Q(out_20), .clr(rst));
  Register #(.width(1)) register_6 (.D(in_6), .en(not_1_out), .clk(clk), .Q(out_21), .clr(rst));
  Register #(.width(1)) register_7 (.D(in_7), .en(not_1_out), .clk(clk), .Q(out_22), .clr(rst));
  Register #(.width(1)) register_8 (.D(in_8), .en(not_1_out), .clk(clk), .Q(out_23), .clr(rst));
  Register #(.width(1)) register_9 (.D(in_9), .en(not_1_out), .clk(clk), .Q(out_24), .clr(rst));
  Register #(.width(4)) register_10 (.D(in_10), .en(not_1_out), .clk(clk), .Q(out_25), .clr(rst));
  Register #(.width(4)) register_11 (.D(in_11), .en(not_1_out), .clk(clk), .Q(out_26), .clr(rst));
  Register #(.width(32)) register_12 (.D(in_12), .en(not_1_out), .clk(clk), .Q(out_27), .clr(rst));
  not not_1 (not_1_out, stall);
  Register #(.width(1)) register_13 (.clk(clk), .Q(register_13_q), .clr(rst));  // open: D, en
endmodule

module alu (
  input  [3:0] opSel,
  input  [31:0] a,
  input  [31:0] b,
  output [31:0] c
);

  wire [15:0] divider_1_out, divider_1_rem;
  wire [31:0] adder_1_out, and_1_out, multiplier_1_out, not_1_out, or_1_out, shifter_1_out, shifter_2_out,
       subtractor_1_out, xor_1_out;

  assign and_1_out = a & b;  // AND_Gate and_1, 32 bits wide
  assign or_1_out = a | b;  // OR_Gate or_1, 32 bits wide
  assign not_1_out = ~a;  // NOT_Gate not_1, 32 bits wide
  assign xor_1_out = a ^ b;  // XOR_Gate xor_1, 32 bits wide
  Adder #(.width(32)) adder_1 (.a(a), .b(b), .out(adder_1_out));  // open: cin, cout
  Subtractor #(.width(32)) subtractor_1 (.a(a), .b(b), .out(subtractor_1_out));  // open: bin, bout
  Multiplier #(.width(32)) multiplier_1 (.a(a), .b(b), .out(multiplier_1_out));  // open: cin, cout
  Divider #(.width(16)) divider_1 (
    .a(a[15:0]), .b(b[15:0]), .out(divider_1_out), .upper(a[31:16]), .rem(divider_1_rem));
  Shifter #(.width(32)) shifter_1 (.in(a), .\dist (b[4:0]), .out(shifter_1_out));
  Shifter #(.shift("lr"), .width(32)) shifter_2 (.in(a), .\dist (b[4:0]), .out(shifter_2_out));
  Multiplexer #(.select(4), .width(32)) multiplexer_1 (
    .in0(and_1_out), .in1(or_1_out), .in2(not_1_out), .in3(xor_1_out), .in4(adder_1_out),
    .in5(subtractor_1_out), .in6(multiplier_1_out), .in7({divider_1_rem, divider_1_out}),
    .in8(shifter_1_out), .in9(shifter_2_out), .out(c), .sel(opSel));  // open: in10, in11, in12, in13, in14, in15
endmodule

module memory (
  input  [31:0] mmapData,
  input  load,
  input  store,
  input  [31:0] addr,
  input  [31:0] dataIn,
  input  clk,
  output mmapDevices,
  output mmapVram,
  output ack,
  output [31:0] dataOut
);

  wire comparator_1_gt, or_2_out;
  wire [31:0] ram_1_dout;

  Comparator #(.mode("unsigned"), .width(32)) comparator_1 (
    .a(32'h4100), .b(addr), .gt(comparator_1_gt));  // open: eq, lt
  Comparator #(.mode("unsigned"), .width(32)) comparator_2 (.a(32'h4000), .b(addr), .gt(mmapVram));  // open: eq, lt
  RAM #(.addrWidth(24), .asyncread("true"), .dataWidth(32)) ram_1 (
    .addr(addr[23:0]), .we(store), .oe(load), .clk(clk), .din(dataIn), .dout(ram_1_dout));
  and and_1 (mmapDevices, comparator_1_gt, ~mmapVram);  // AND_Gate
  or or_1 (ack, load, store);
  or or_2 (or_2_out, mmapVram, mmapDevices);
  Multiplexer #(.width(32)) multiplexer_1 (.in0(mmapData), .in1(ram_1_dout), .out(dataOut), .sel(or_2_out));
endmodule
